# Fritzing sketch WeMos_Voltage_Devider (saved by Fritzing 0.9.3b)
breadboards: 1

parts:
  R1 = Resistor [tolerance=±5% resistance=10k package=THT]
  R2 = Resistor [tolerance=±5% resistance=10k package=THT]
  WeMos_D1_Mini1 = WeMos D1 Mini  # not connected

nets:
  N1: R1.Pin_1, R2.Pin_0
